# Fritzing sketch GPSSchematic (saved by Fritzing 0.9.3b)
breadboards: 1

parts:
  Part1 = Arduino Nano (Rev3.0)
  GY-NEO6MV3 = SUP500F [package=sup500f]
  Part3 = PowerBoost 500 Charger
  U1 = LIPO-1000mAh [package=lipo-1000]
  Part2 = MicroSD Card Module

nets:
  N1: Part1.D0/RX, GY-NEO6MV3.TX-O
  GND: Part1.GND, GY-NEO6MV3.GND, Part3.GND, Part2.GND
  N2: Part1.D4, Part2.CS
  N3: Part1.D11/MOSI, Part2.MOSI
  N4: Part1.D12/MISO, Part2.MISO
  VCC: Part1.5V, GY-NEO6MV3.VCC, Part3.5.0V, Part2.VCC
  N5: Part1.D13/SCK, Part2.SCK
  N6: Part3.GND_BAT_IN, U1.-
  N7: Part3.VBAT_IN, U1.+

notes:
  GND: Black
  VCC: Red
  TX: Purple
  GND: Black
  VCC: Red
  MISO: Brown
  MOSI: Orange
  SCK: Grey
  CS: Green
